// Digital circuit UTS-2.dig as structural Verilog
module UTS_2 (
  input  A,
  input  B,
  input  C,
  input  D,
  output X
);

  wire and_2_out, and_3_out, and_4_out, and_5_out, not_1_out, not_3_out, not_4_out;

  not not_1 (not_1_out, A);
  not not_2 (A, B);
  not not_3 (not_3_out, B);
  not not_4 (not_4_out, A);
  buf and_1 (A, A);  // And open: In_1, In_3
  buf and_2 (and_2_out, B);  // And open: In_1, In_3
  and and_3 (and_3_out, not_3_out, not_4_out);  // open: In_2
  and and_4 (and_4_out, not_1_out, A);  // open: In_3
  buf and_5 (and_5_out, and_2_out);  // And open: In_1, In_3
  // And and_6 has open pins: In_1=A, In_2=A, In_3=open, out=open
  or or_1 (X, and_5_out, and_3_out, and_3_out, and_3_out);  // open: In_1, In_4

  assign C = B;
  assign D = A;

  // Notes on the sheet:
  //   NASYABILLA ARIVIA F
endmodule
